# Fritzing sketch MoPhong_DongHo_LCD (saved by Fritzing 0.9.3b)
circuit board: 8.46667cm x 5.64444cm

parts:
  LCM1602_IIC1 = LCM1602 IIC [part_number="LCM1602 IIC" chip_label="LCM1602 IIC" package="DIP (Dual Inline) [THT]"]
  LCD1 = LCD screen
  Linh_kiện1 = Arduino Uno (Rev3) - ICSP
  Linh_kiện2 = Real Time Clock Module - DS1307 RTC Breakout Board

nets:
  VSS: LCM1602_IIC1.VSS, LCD1.VSS
  VDD: LCM1602_IIC1.VDD, LCD1.VDD
  N1: LCM1602_IIC1.V0, LCD1.V0
  N2: LCM1602_IIC1.RS, LCD1.RS
  N3: LCM1602_IIC1.RW, LCD1.R/W
  N4: LCM1602_IIC1.E, LCD1.E
  N5: LCM1602_IIC1.D0, LCD1.DB0
  N6: LCM1602_IIC1.D1, LCD1.DB1
  N7: LCM1602_IIC1.D2, LCD1.DB2
  N8: LCM1602_IIC1.D3, LCD1.DB3
  N9: LCM1602_IIC1.D4, LCD1.DB4
  N10: LCM1602_IIC1.D5, LCD1.DB5
  N11: LCM1602_IIC1.D6, LCD1.DB6
  N12: LCM1602_IIC1.D7, LCD1.DB7
  N13: LCM1602_IIC1.A, LCD1.LED+
  N14: LCM1602_IIC1.K, LCD1.LED-
  GND: LCM1602_IIC1.GND, Linh_kiện1.GND, Linh_kiện2.GND
  5V: LCM1602_IIC1.VCC, Linh_kiện1.5V, Linh_kiện2.5V
  N15: LCM1602_IIC1.SDA, Linh_kiện1.A5/SCL, Linh_kiện2.SCL
  N16: LCM1602_IIC1.SCL, Linh_kiện1.A4/SDA, Linh_kiện2.SDA

notes:
  Arduino Uno
  LCD 16x2
  DS1307
  I2C LCD

custom parts:
  LCM1602 IIC: I2C-Module to use a 1602 or 2004 LCD on with the wire.h libory Serial LCD Modul

// code stored in the sketch: DongHo_LCD.fzz.ino
//Khai báo th? vi?n s? d?ng
#include <Wire.h>
#include "RTClib.h"
#include <LiquidCrystal_I2C.h>
//Khai báo th?i gian th?c
RTC_DS1307 rtc;
//??a ch? màn hình 0x27, (16x2): 16 c?t, 2 hàng 
LiquidCrystal_I2C lcd(0x27,16,2);
//Khai báo các bi?n ?? l?y giá tr? th?i gian
int thu, ngay, thang, nam, gio, phut, giay;
void setup() 
{
	//Giá tr? t?c ?? truy?n thông n?i ti?p 9600
	Serial.begin(9600);
	//Kh?i ??ng màn hình
	lcd.init();  
	//B?t ?èn n?n
	lcd.backlight();
	//Kh?i t?o RTC
	if (! rtc.begin()) 
	{	
		//Thông báo lên màn hình Serial Monitor
		Serial.print("Khong tim thay RTC !");
		//Thông báo lên màn hình LCD
		lcd.print("Khong tim thay RTC!");
		while (1);
	}
	if (! rtc.isrunning()) 
	{
		Serial.print("RTC khong chay!");
		lcd.print("RTC khong chay!");
	}
	//Cách 1: C?p nh?t th?i gian l?n ??u cho DS1307 t? máy tính
	rtc.adjust(DateTime(F(__DATE__), F(__TIME__)));
	//Cách 2: Thi?t l?p gi? th? công
    //rtc.adjust(DateTime(2020, 1, 15, 8, 15, 0));
}
void loop () 
{
	//Thi?t l?p th?i gian hi?n t?i
    DateTime now = rtc.now();
	//Truy?n giá tr? cho các bi?n th?, ngày, tháng, n?m
	thu = now.dayOfTheWeek();
	ngay = now.day();
	thang = now.month();
	nam = now.year();
	//Truy?n giá tr? cho các bi?n th?, ngày, tháng, n?m
	gio = now.hour();
	phut = now.minute();
	giay = now.second();
	//Hàng ??u tiên hi?n th? th?, ngày, tháng, n?m
    lcd.setCursor(0, 0);
	//Hi?n th? th? trong tu?n
    switch(thu)
	{
		case 0:
			lcd.print("CN,");
			break;
		case 1:
			lcd.print("Thu 2,");
			break;
		case 2:
			lcd.print("Thu 3,");
			break;
		case 3:
			lcd.print("Thu 4,");
			break;
		case 4:
			lcd.print("Thu 5,");
			break;
		case 5:
			lcd.print("Thu 6,");
			break;
		case 6:
			lcd.print("Thu 7,");
			break;			
	}
	//Hi?n th? ngày
	if(ngay <= 9)	//Các ?i?u ki?n in th?i gian th?, ngày/tháng/n?m
    {
		lcd.print("0");
		lcd.print(ngay);
    }
    else
		lcd.print(ngay); 
    
    lcd.print('/');	//D?u / phân cách gi?a ngày/tháng/n?m
	//Hi?n th? tháng
    if(thang <= 9)
    {
		lcd.print("0");
		lcd.print(thang);
    }
    else
		lcd.print(thang); 
    //Hi?n th? n?m
    lcd.print('/');
    if(nam <= 9)
    {
		lcd.print("0");
		lcd.print(nam);
    }
    else 
		lcd.print(nam); 
	//
	//Hàng 2 hi?n th? thông tin gi?/phút/giây
	lcd.setCursor(0, 1);
	lcd.print("TIME: ");
	//Hi?n th? gi?
    if(gio <= 9)	//?i?u ki?n hi?n th?
    {
      lcd.print("0");
      lcd.print(gio);
    }
    else
     lcd.print(gio); 
    lcd.print(':');	//D?u : phân cách gi?a gi?/phút/giây
	//Hi?n  th? phút
    if(phut <= 9)
    {
      lcd.print("0");
      lcd.print(phut);
    }
    else
     lcd.print(phut); 
    
    lcd.print(':');
	//Hi?n  th? giây
    if(giay <= 9)	
    {
      lcd.print("0");
      lcd.print(giay);
    }
    else
     lcd.print(giay); 
    
}
